# Fritzing sketch RPi_USBtoTLL (saved by Fritzing 0.9.3b)

parts:
  Raspberry_Pi_1 = Raspberry Pi 3 [part_number=RPI-3-V1.2]
  Bauteil1 = XBee USB Mini Adapter

nets:
  N1: Raspberry_Pi_1.GPIO15, Bauteil1.TXD
  N2: Raspberry_Pi_1.GPIO14, Bauteil1.RXD
  GND: Raspberry_Pi_1.GND, Bauteil1.GND
  5V: Raspberry_Pi_1.5V, Bauteil1.5V
