# Fritzing sketch RPi_USBtoTLL_complete (saved by Fritzing 0.9.3b)

parts:
  Bauteil1 = XBee USB Mini Adapter
  Raspberry_Pi_1 = Raspberry Pi 3 [part_number=RPI-3-V1.2]
  Gesture_Sensor = ZX Sensor [chip_label=IC package="DIP (Dual Inline) [THT]"]

nets:
  N1: Bauteil1.RXD, Raspberry_Pi_1.GPIO4, Raspberry_Pi_1.GPIO14
  GND: Bauteil1.TXD, Bauteil1.GND, Raspberry_Pi_1.GND, Raspberry_Pi_1.GPIO15, Gesture_Sensor.pin5
  5V: Bauteil1.5V, Raspberry_Pi_1.5V
  N2: Raspberry_Pi_1.GPIO2, Gesture_Sensor.pin_9
  N3: Raspberry_Pi_1.GPIO3, Gesture_Sensor.pin8
  N4: Raspberry_Pi_1.3V3, Gesture_Sensor.pin4

custom parts:
  ZX Sensor: A DIP stand-in part for whatever IC you want. With 8 pins on a 300mil dual inline package (DIP) footprint.
